// Logisim project branch-comp.circ as structural Verilog: 1 circuit, main circuit branch_comp
module branch_comp (
  input  [31:0] BrData1,
  input  [31:0] BrData2,
  input  BrUn,
  output BrEq,
  output BrLt
);

  wire S_BrEq, S_BrLt, U_BrEq, U_BrLt;

  Comparator #(.width(32)) comparator_1 (.a(BrData1), .b(BrData2), .eq(S_BrEq), .lt(S_BrLt));  // open: gt
  Comparator #(.mode("unsigned"), .width(32)) comparator_2 (
    .a(BrData1), .b(BrData2), .eq(U_BrEq), .lt(U_BrLt));  // open: gt
  Multiplexer #(.enable("false")) multiplexer_1 (.in0(S_BrEq), .in1(U_BrEq), .out(BrEq), .sel(BrUn));
  Multiplexer #(.enable("false")) multiplexer_2 (.in0(S_BrLt), .in1(U_BrLt), .out(BrLt), .sel(BrUn));

  // Notes on the sheet:
  //   INPUTS to your circuit
  //   DON'T CHANGE THE LOCATIONS OF THE INPUTS AND OUTPUTS!
  //   OUTPUT from your circuit
endmodule
