// Logisim project control-logic.circ as structural Verilog: 1 circuit, main circuit control_logic
module control_logic (
  input  [31:0] Instruction,
  input  BrEq,
  input  BrLt,
  output PCSel,
  output RegWEn,
  output [2:0] ImmSel,
  output BrUn,
  output ASel,
  output BSel,
  output [3:0] ALUSel,
  output MemWEn,
  output [1:0] WBSel
);

  wire add_0, addi_15, and_1_out, and_3_out, and_5_out, and_7_out, and_11, and_17_out, and_18_out,
       and_19_out, and_20_out, and_22_out, and_23_out, and_34_out, and_35_out, and_36_out, and_37_out,
       and_38_out, and_39_out, and_40_out, and_41_out, and_42_out, and_43_out, and_46_out, andi_22, auipc_32,
       beq_26, bge_29, bgeu_31, blt_28, bltu_30, bne_27, comparator_1_eq, comparator_2_eq, comparator_3_eq,
       comparator_4_eq, comparator_5_eq, comparator_6_eq, comparator_7_eq, comparator_8_eq, comparator_9_eq,
       comparator_10_eq, comparator_11_eq, comparator_12_eq, comparator_13_eq, comparator_14_eq,
       comparator_15_eq, comparator_16_eq, comparator_17_eq, comparator_18_eq, comparator_19_eq,
       comparator_20_eq, comparator_21_eq, comparator_22_eq, comparator_23_eq, comparator_24_eq,
       comparator_25_eq, comparator_26_eq, comparator_29_eq, comparator_30_eq, comparator_31_eq,
       comparator_32_eq, comparator_33_eq, comparator_34_eq, comparator_35_eq, comparator_36_eq,
       comparator_37_eq, comparator_38_eq, comparator_39_eq, comparator_40_eq, comparator_41_eq,
       comparator_42_eq, comparator_43_eq, comparator_44_eq, comparator_45_eq, comparator_46_eq,
       comparator_47_eq, comparator_48_eq, comparator_49_eq, comparator_50_eq, comparator_51_eq,
       comparator_52_eq, comparator_53_eq, comparator_54_eq, comparator_55_eq, comparator_56_eq,
       comparator_57_eq, comparator_58_eq, comparator_60_eq, comparator_61_eq, comparator_62_eq,
       comparator_63_eq, comparator_64_eq, comparator_65_eq, comparator_66_eq, comparator_67_eq,
       comparator_68_eq, comparator_69_eq, comparator_70_eq, comparator_71_eq, comparator_72_eq,
       comparator_73_eq, comparator_74_eq, comparator_75_eq, comparator_76_eq, comparator_77_eq,
       comparator_78_eq, comparator_79_eq, comparator_80_eq, comparator_81_eq, comparator_82_eq,
       comparator_83_eq, comparator_84_eq, jal_34, jalr_35, lb_12, lh_13, lui_33, lw_14, mul_1, mulh_4,
       mulhu_5, not_1_out, not_2_out, not_3_out, or_1_out, or_2_out, or_3_out, or_4_out, or_5_out, or_6_out,
       or_10, ori_21, priority_encoder_1_gs, sb_23, sh_24, sll_3, slli_16, slt_6, slti_17, sra_9, srai_20,
       srl_8, srli_19, sub_2, sw_25, xor_7, xori_18;
  wire [1:0] ROM_input2;
  wire [4:0] priority_encoder_1_out;
  wire [5:0] ROM_input, ROM_input1;
  wire [15:14] rom_1_data;

  Comparator #(.width(5)) comparator_1 (.a(Instruction[6:2]), .b(5'b01100), .eq(comparator_1_eq));  // open: gt, lt
  Comparator #(.width(3)) comparator_2 (.a(Instruction[14:12]), .b(3'b000), .eq(comparator_2_eq));  // open: gt, lt
  Comparator #(.width(7)) comparator_3 (.a(Instruction[31:25]), .b({7{1'b0}}), .eq(comparator_3_eq));  // open: gt, lt
  Comparator #(.width(5)) comparator_4 (.a(Instruction[6:2]), .b(5'b01100), .eq(comparator_4_eq));  // open: gt, lt
  Comparator #(.width(3)) comparator_5 (.a(Instruction[14:12]), .b(3'b001), .eq(comparator_5_eq));  // open: gt, lt
  Comparator #(.width(7)) comparator_6 (.a(Instruction[31:25]), .b({7{1'b0}}), .eq(comparator_6_eq));  // open: gt, lt
  Comparator #(.width(5)) comparator_7 (.a(Instruction[6:2]), .b(5'b01100), .eq(comparator_7_eq));  // open: gt, lt
  Comparator #(.width(3)) comparator_8 (.a(Instruction[14:12]), .b(3'b010), .eq(comparator_8_eq));  // open: gt, lt
  Comparator #(.width(7)) comparator_9 (.a(Instruction[31:25]), .b({7{1'b0}}), .eq(comparator_9_eq));  // open: gt, lt
  Comparator #(.width(5)) comparator_10 (.a(Instruction[6:2]), .b(5'b01100), .eq(comparator_10_eq));  // open: gt, lt
  Comparator #(.width(3)) comparator_11 (.a(Instruction[14:12]), .b(3'b101), .eq(comparator_11_eq));  // open: gt, lt
  Comparator #(.width(7)) comparator_12 (
    .a(Instruction[31:25]), .b(7'b0100000), .eq(comparator_12_eq));  // open: gt, lt
  Comparator #(.width(5)) comparator_13 (.a(Instruction[6:2]), .b({5{1'b0}}), .eq(comparator_13_eq));  // open: gt, lt
  Comparator #(.width(3)) comparator_14 (.a(Instruction[14:12]), .b(3'b000), .eq(comparator_14_eq));  // open: gt, lt
  Comparator #(.width(5)) comparator_15 (.a(Instruction[6:2]), .b(5'b00100), .eq(comparator_15_eq));  // open: gt, lt
  Comparator #(.width(3)) comparator_16 (.a(Instruction[14:12]), .b(3'b000), .eq(comparator_16_eq));  // open: gt, lt
  Comparator #(.width(5)) comparator_17 (.a(Instruction[6:2]), .b(5'b00100), .eq(comparator_17_eq));  // open: gt, lt
  Comparator #(.width(3)) comparator_18 (.a(Instruction[14:12]), .b(3'b100), .eq(comparator_18_eq));  // open: gt, lt
  Comparator #(.width(5)) comparator_19 (.a(Instruction[6:2]), .b(5'b00100), .eq(comparator_19_eq));  // open: gt, lt
  Comparator #(.width(3)) comparator_20 (.a(Instruction[14:12]), .b(3'b110), .eq(comparator_20_eq));  // open: gt, lt
  Comparator #(.width(5)) comparator_21 (.a(Instruction[6:2]), .b(5'b01000), .eq(comparator_21_eq));  // open: gt, lt
  Comparator #(.width(3)) comparator_22 (.a(Instruction[14:12]), .b(3'b000), .eq(comparator_22_eq));  // open: gt, lt
  Comparator #(.width(5)) comparator_23 (.a(Instruction[6:2]), .b(5'b11000), .eq(comparator_23_eq));  // open: gt, lt
  Comparator #(.width(3)) comparator_24 (.a(Instruction[14:12]), .b(3'b000), .eq(comparator_24_eq));  // open: gt, lt
  Comparator #(.width(5)) comparator_25 (.a(Instruction[6:2]), .b(5'b11000), .eq(comparator_25_eq));  // open: gt, lt
  Comparator #(.width(3)) comparator_26 (.a(Instruction[14:12]), .b(3'b101), .eq(comparator_26_eq));  // open: gt, lt
  Comparator #(.width(5)) comparator_27 (.a(Instruction[6:2]), .b(5'b00101), .eq(auipc_32));  // open: gt, lt
  Comparator #(.width(5)) comparator_28 (.a(Instruction[6:2]), .b(5'b11011), .eq(jal_34));  // open: gt, lt
  Comparator #(.width(5)) comparator_29 (.a(Instruction[6:2]), .b(5'b11001), .eq(comparator_29_eq));  // open: gt, lt
  Comparator #(.width(3)) comparator_30 (.a(Instruction[14:12]), .b(3'b000), .eq(comparator_30_eq));  // open: gt, lt
  ROM #(.addrWidth(6), .dataWidth(16)) rom_1 (
    .addr(ROM_input), .data({rom_1_data, WBSel, MemWEn, ALUSel, BSel, ASel, BrUn, ImmSel, RegWEn}));
  and and_1 (and_1_out, comparator_1_eq, comparator_2_eq);
  and and_2 (add_0, and_1_out, comparator_3_eq);
  and and_3 (and_3_out, comparator_4_eq, comparator_5_eq);
  and and_4 (sll_3, and_3_out, comparator_6_eq);
  and and_5 (and_5_out, comparator_7_eq, comparator_8_eq);
  and and_6 (slt_6, and_5_out, comparator_9_eq);
  and and_7 (and_7_out, comparator_10_eq, comparator_11_eq);
  and and_8 (sra_9, and_7_out, comparator_12_eq);
  and and_9 (lb_12, comparator_13_eq, comparator_14_eq);
  and and_10 (addi_15, comparator_15_eq, comparator_16_eq);
  and u_and_11 (xori_18, comparator_17_eq, comparator_18_eq);
  and and_12 (ori_21, comparator_19_eq, comparator_20_eq);
  and and_13 (sb_23, comparator_21_eq, comparator_22_eq);
  and and_14 (beq_26, comparator_23_eq, comparator_24_eq);
  and and_15 (bge_29, comparator_25_eq, comparator_26_eq);
  and and_16 (jalr_35, comparator_29_eq, comparator_30_eq);
  Priority_Encoder #(.select(5)) priority_encoder_1 (
    .in0(add_0), .in1(mul_1), .in2(sub_2), .in3(sll_3), .in4(mulh_4), .in5(mulhu_5), .in6(slt_6),
    .in7(xor_7), .in8(srl_8), .in9(sra_9), .in10(or_10), .in11(and_11), .in12(lb_12), .in13(lh_13),
    .in14(lw_14), .in15(addi_15), .in16(slli_16), .in17(slti_17), .in18(xori_18), .in19(srli_19),
    .in20(srai_20), .in21(ori_21), .in22(andi_22), .in23(sb_23), .in24(sh_24), .in25(sw_25), .in26(beq_26),
    .in27(bne_27), .in28(blt_28), .in29(bge_29), .in30(bltu_30), .in31(bgeu_31),
    .out(priority_encoder_1_out), .gs(priority_encoder_1_gs));  // open: en_out, en_in
  Priority_Encoder #(.select(2)) priority_encoder_2 (
    .in0(auipc_32), .in1(lui_33), .in2(jal_34), .in3(jalr_35), .out(ROM_input2));  // open: gs, en_out, en_in
  assign ROM_input1 = {{1{1'b0}}, priority_encoder_1_out};  // Bit_Extender bit_extender_1
  Comparator #(.width(5)) comparator_31 (.a(Instruction[6:2]), .b(5'b01100), .eq(comparator_31_eq));  // open: gt, lt
  Comparator #(.width(3)) comparator_32 (.a(Instruction[14:12]), .b(3'b000), .eq(comparator_32_eq));  // open: gt, lt
  Comparator #(.width(7)) comparator_33 (
    .a(Instruction[31:25]), .b(7'b0000001), .eq(comparator_33_eq));  // open: gt, lt
  Comparator #(.width(5)) comparator_34 (.a(Instruction[6:2]), .b(5'b01100), .eq(comparator_34_eq));  // open: gt, lt
  Comparator #(.width(3)) comparator_35 (.a(Instruction[14:12]), .b(3'b001), .eq(comparator_35_eq));  // open: gt, lt
  Comparator #(.width(7)) comparator_36 (
    .a(Instruction[31:25]), .b(7'b0000001), .eq(comparator_36_eq));  // open: gt, lt
  Comparator #(.width(5)) comparator_37 (.a(Instruction[6:2]), .b(5'b01100), .eq(comparator_37_eq));  // open: gt, lt
  Comparator #(.width(3)) comparator_38 (.a(Instruction[14:12]), .b(3'b100), .eq(comparator_38_eq));  // open: gt, lt
  Comparator #(.width(7)) comparator_39 (.a(Instruction[31:25]), .b({7{1'b0}}), .eq(comparator_39_eq));  // open: gt, lt
  Comparator #(.width(5)) comparator_40 (.a(Instruction[6:2]), .b(5'b01100), .eq(comparator_40_eq));  // open: gt, lt
  Comparator #(.width(3)) comparator_41 (.a(Instruction[14:12]), .b(3'b110), .eq(comparator_41_eq));  // open: gt, lt
  Comparator #(.width(7)) comparator_42 (.a(Instruction[31:25]), .b({7{1'b0}}), .eq(comparator_42_eq));  // open: gt, lt
  Comparator #(.width(5)) comparator_43 (.a(Instruction[6:2]), .b({5{1'b0}}), .eq(comparator_43_eq));  // open: gt, lt
  Comparator #(.width(3)) comparator_44 (.a(Instruction[14:12]), .b(3'b001), .eq(comparator_44_eq));  // open: gt, lt
  Comparator #(.width(5)) comparator_45 (.a(Instruction[6:2]), .b(5'b00100), .eq(comparator_45_eq));  // open: gt, lt
  Comparator #(.width(3)) comparator_46 (.a(Instruction[14:12]), .b(3'b001), .eq(comparator_46_eq));  // open: gt, lt
  Comparator #(.width(7)) comparator_47 (.a(Instruction[31:25]), .b({7{1'b0}}), .eq(comparator_47_eq));  // open: gt, lt
  Comparator #(.width(5)) comparator_48 (.a(Instruction[6:2]), .b(5'b00100), .eq(comparator_48_eq));  // open: gt, lt
  Comparator #(.width(3)) comparator_49 (.a(Instruction[14:12]), .b(3'b101), .eq(comparator_49_eq));  // open: gt, lt
  Comparator #(.width(7)) comparator_50 (.a(Instruction[31:25]), .b({7{1'b0}}), .eq(comparator_50_eq));  // open: gt, lt
  Comparator #(.width(5)) comparator_51 (.a(Instruction[6:2]), .b(5'b00100), .eq(comparator_51_eq));  // open: gt, lt
  Comparator #(.width(3)) comparator_52 (.a(Instruction[14:12]), .b(3'b111), .eq(comparator_52_eq));  // open: gt, lt
  Comparator #(.width(5)) comparator_53 (.a(Instruction[6:2]), .b(5'b01000), .eq(comparator_53_eq));  // open: gt, lt
  Comparator #(.width(3)) comparator_54 (.a(Instruction[14:12]), .b(3'b001), .eq(comparator_54_eq));  // open: gt, lt
  Comparator #(.width(5)) comparator_55 (.a(Instruction[6:2]), .b(5'b11000), .eq(comparator_55_eq));  // open: gt, lt
  Comparator #(.width(3)) comparator_56 (.a(Instruction[14:12]), .b(3'b001), .eq(comparator_56_eq));  // open: gt, lt
  Comparator #(.width(5)) comparator_57 (.a(Instruction[6:2]), .b(5'b11000), .eq(comparator_57_eq));  // open: gt, lt
  Comparator #(.width(3)) comparator_58 (.a(Instruction[14:12]), .b(3'b110), .eq(comparator_58_eq));  // open: gt, lt
  Comparator #(.width(5)) comparator_59 (.a(Instruction[6:2]), .b(5'b01101), .eq(lui_33));  // open: gt, lt
  and and_17 (and_17_out, comparator_31_eq, comparator_32_eq);
  and and_18 (and_18_out, comparator_34_eq, comparator_35_eq);
  and and_19 (and_19_out, comparator_37_eq, comparator_38_eq);
  and and_20 (and_20_out, comparator_40_eq, comparator_41_eq);
  and and_21 (lh_13, comparator_43_eq, comparator_44_eq);
  and and_22 (and_22_out, comparator_45_eq, comparator_46_eq);
  and and_23 (and_23_out, comparator_48_eq, comparator_49_eq);
  and and_24 (andi_22, comparator_51_eq, comparator_52_eq);
  and and_25 (sh_24, comparator_53_eq, comparator_54_eq);
  and and_26 (bne_27, comparator_55_eq, comparator_56_eq);
  and and_27 (bltu_30, comparator_57_eq, comparator_58_eq);
  and and_28 (mul_1, and_17_out, comparator_33_eq);
  and and_29 (mulh_4, and_18_out, comparator_36_eq);
  and and_30 (xor_7, and_19_out, comparator_39_eq);
  and and_31 (or_10, and_20_out, comparator_42_eq);
  and and_32 (slli_16, and_22_out, comparator_47_eq);
  and and_33 (srli_19, and_23_out, comparator_50_eq);
  not not_1 (not_1_out, BrEq);
  not not_2 (not_2_out, BrLt);
  not not_3 (not_3_out, BrLt);
  Multiplexer #(.enable("false"), .width(6)) multiplexer_1 (
    .in0({4'b1000, ROM_input2}), .in1(ROM_input1), .out(ROM_input), .sel(priority_encoder_1_gs));
  and and_34 (and_34_out, beq_26, BrEq);
  and and_35 (and_35_out, bne_27, not_1_out);
  and and_36 (and_36_out, blt_28, BrLt);
  and and_37 (and_37_out, bge_29, not_2_out);
  and and_38 (and_38_out, bltu_30, BrLt);
  and and_39 (and_39_out, bgeu_31, not_3_out);
  or or_1 (or_1_out, and_34_out, and_35_out);
  or or_2 (or_2_out, and_36_out, and_37_out);
  or or_3 (or_3_out, and_38_out, and_39_out);
  or or_4 (or_4_out, jal_34, jalr_35);
  Comparator #(.width(5)) comparator_60 (.a(Instruction[6:2]), .b(5'b01100), .eq(comparator_60_eq));  // open: gt, lt
  Comparator #(.width(3)) comparator_61 (.a(Instruction[14:12]), .b(3'b000), .eq(comparator_61_eq));  // open: gt, lt
  Comparator #(.width(7)) comparator_62 (
    .a(Instruction[31:25]), .b(7'b0100000), .eq(comparator_62_eq));  // open: gt, lt
  Comparator #(.width(5)) comparator_63 (.a(Instruction[6:2]), .b(5'b01100), .eq(comparator_63_eq));  // open: gt, lt
  Comparator #(.width(3)) comparator_64 (.a(Instruction[14:12]), .b(3'b011), .eq(comparator_64_eq));  // open: gt, lt
  Comparator #(.width(7)) comparator_65 (
    .a(Instruction[31:25]), .b(7'b0000001), .eq(comparator_65_eq));  // open: gt, lt
  Comparator #(.width(5)) comparator_66 (.a(Instruction[6:2]), .b(5'b01100), .eq(comparator_66_eq));  // open: gt, lt
  Comparator #(.width(3)) comparator_67 (.a(Instruction[14:12]), .b(3'b101), .eq(comparator_67_eq));  // open: gt, lt
  Comparator #(.width(7)) comparator_68 (.a(Instruction[31:25]), .b({7{1'b0}}), .eq(comparator_68_eq));  // open: gt, lt
  Comparator #(.width(5)) comparator_69 (.a(Instruction[6:2]), .b(5'b01100), .eq(comparator_69_eq));  // open: gt, lt
  Comparator #(.width(3)) comparator_70 (.a(Instruction[14:12]), .b(3'b111), .eq(comparator_70_eq));  // open: gt, lt
  Comparator #(.width(7)) comparator_71 (.a(Instruction[31:25]), .b({7{1'b0}}), .eq(comparator_71_eq));  // open: gt, lt
  Comparator #(.width(5)) comparator_72 (.a(Instruction[6:2]), .b({5{1'b0}}), .eq(comparator_72_eq));  // open: gt, lt
  Comparator #(.width(3)) comparator_73 (.a(Instruction[14:12]), .b(3'b010), .eq(comparator_73_eq));  // open: gt, lt
  Comparator #(.width(5)) comparator_74 (.a(Instruction[6:2]), .b(5'b00100), .eq(comparator_74_eq));  // open: gt, lt
  Comparator #(.width(3)) comparator_75 (.a(Instruction[14:12]), .b(3'b010), .eq(comparator_75_eq));  // open: gt, lt
  Comparator #(.width(5)) comparator_76 (.a(Instruction[6:2]), .b(5'b00100), .eq(comparator_76_eq));  // open: gt, lt
  Comparator #(.width(3)) comparator_77 (.a(Instruction[14:12]), .b(3'b101), .eq(comparator_77_eq));  // open: gt, lt
  Comparator #(.width(7)) comparator_78 (
    .a(Instruction[31:25]), .b(7'b0100000), .eq(comparator_78_eq));  // open: gt, lt
  Comparator #(.width(5)) comparator_79 (.a(Instruction[6:2]), .b(5'b01000), .eq(comparator_79_eq));  // open: gt, lt
  Comparator #(.width(3)) comparator_80 (.a(Instruction[14:12]), .b(3'b010), .eq(comparator_80_eq));  // open: gt, lt
  Comparator #(.width(5)) comparator_81 (.a(Instruction[6:2]), .b(5'b11000), .eq(comparator_81_eq));  // open: gt, lt
  Comparator #(.width(3)) comparator_82 (.a(Instruction[14:12]), .b(3'b100), .eq(comparator_82_eq));  // open: gt, lt
  Comparator #(.width(5)) comparator_83 (.a(Instruction[6:2]), .b(5'b11000), .eq(comparator_83_eq));  // open: gt, lt
  Comparator #(.width(3)) comparator_84 (.a(Instruction[14:12]), .b(3'b111), .eq(comparator_84_eq));  // open: gt, lt
  or or_5 (or_5_out, or_1_out, or_2_out);
  or or_6 (or_6_out, or_3_out, or_4_out);
  and and_40 (and_40_out, comparator_60_eq, comparator_61_eq);
  and and_41 (and_41_out, comparator_63_eq, comparator_64_eq);
  and and_42 (and_42_out, comparator_66_eq, comparator_67_eq);
  and and_43 (and_43_out, comparator_69_eq, comparator_70_eq);
  and and_44 (lw_14, comparator_72_eq, comparator_73_eq);
  and and_45 (slti_17, comparator_74_eq, comparator_75_eq);
  and and_46 (and_46_out, comparator_76_eq, comparator_77_eq);
  and and_47 (sw_25, comparator_79_eq, comparator_80_eq);
  and and_48 (blt_28, comparator_81_eq, comparator_82_eq);
  and and_49 (bgeu_31, comparator_83_eq, comparator_84_eq);
  or or_7 (PCSel, or_5_out, or_6_out);
  and and_50 (sub_2, and_40_out, comparator_62_eq);
  and and_51 (mulhu_5, and_41_out, comparator_65_eq);
  and and_52 (srl_8, and_42_out, comparator_68_eq);
  and and_53 (and_11, and_43_out, comparator_71_eq);
  and and_54 (srai_20, and_46_out, comparator_78_eq);

  // Other names for the same wires on the sheet: opcode[4:0] = Instruction[6:2]; funct3[2:0] = Instruction[14:12];
  //   funct7[6:0] = Instruction[31:25]

  // Notes on the sheet:
  //   INPUTS to your circuit
  //   contents of rom_1 (hex, n*v repeats v):
  //   1001 1401 1601 1081 1481 1581 1101 1201 1281 1681 1301 1381 41 41 41 1041 10c1 1141 1241 12c1 16c1
  //   1341 13c1 842 842 842 4*64 74 74 1067 17e7 2069 2041
  //   ROM FOR CONTROL LOGIC
  //   DON'T CHANGE THE LOCATIONS OF THE INPUTS AND OUTPUTS!
  //   CONNECT
  //   WIRE
  //   TO
  //   USE
  //   ROM
  //   OUTPUT from your circuit
endmodule
