// Logisim project cpu.circ as structural Verilog: 1 circuit, main circuit cpu
module cpu (
  input  clk,
  input  [31:0] Instruction,
  input  [31:0] MemReadData,
  output [31:0] MemAddress,
  output [31:0] ProgramCounter,
  output [31:0] ra,
  output [31:0] sp,
  output [31:0] t0,
  output [31:0] t1,
  output [31:0] t2,
  output [31:0] s0,
  output [31:0] s1,
  output [31:0] a0,
  output [3:0] MemWriteMask,
  output [31:0] MemWriteData
);

  wire ASel, BrEq, BrLt, BrUn, BSel, MemWEn, PCSel, RegWEn;
  wire [1:0] WBSel;
  wire [2:0] ImmSel;
  wire [3:0] control_logic_1_alusel;
  wire [31:0] imm_gen_1_immediate, Instruction_P, multiplexer_1_out, multiplexer_2_out, multiplexer_3_out,
       multiplexer_4_out, multiplexer_5_out, PC4, PC4_P, ProgramCounter_P, ReadData, RegReadData1,
       RegReadData2;

  Adder #(.width(32)) adder_1 (.a(ProgramCounter), .b(32'h4), .out(PC4));  // open: cin, cout
  Multiplexer #(.enable("false"), .width(32)) multiplexer_1 (
    .in0(PC4), .in1(MemAddress), .out(multiplexer_1_out), .sel(PCSel));
  Register #(.width(32)) register_1 (.D(ProgramCounter), .clk(clk), .Q(ProgramCounter_P));  // open: en, clr
  Register #(.width(32)) register_2 (.D(PC4), .clk(clk), .Q(PC4_P));  // open: en, clr
  Register #(.width(32)) register_3 (.D(multiplexer_2_out), .clk(clk), .Q(Instruction_P));  // open: en, clr
  Multiplexer #(.enable("false"), .width(32)) multiplexer_2 (
    .in0(Instruction), .in1(32'h13), .out(multiplexer_2_out), .sel(PCSel));
  Register #(.width(32)) PC (.D(multiplexer_1_out), .clk(clk), .Q(ProgramCounter));  // open: en, clr
  Multiplexer #(.enable("false"), .select(2), .width(32)) multiplexer_3 (
    .in0(ReadData), .in1(MemAddress), .in2(PC4_P), .out(multiplexer_3_out), .sel(WBSel));  // open: in3
  control_logic control_logic_1 (
    .PCSel(PCSel), .RegWEn(RegWEn), .ImmSel(ImmSel), .BrUn(BrUn), .ASel(ASel), .BSel(BSel),
    .ALUSel(control_logic_1_alusel), .MemWEn(MemWEn), .WBSel(WBSel), .Instruction(Instruction_P),
    .BrEq(BrEq), .BrLt(BrLt));
  regfile regfile_1 (
    .ReadReg1(Instruction_P[19:15]), .ReadReg2(Instruction_P[24:20]), .WriteReg(Instruction_P[11:7]),
    .RegWriteData(multiplexer_3_out), .RegWEn(RegWEn), .clk(clk), .ra(ra), .sp(sp), .t0(t0), .t1(t1),
    .t2(t2), .s0(s0), .s1(s1), .a0(a0), .RegReadData1(RegReadData1), .RegReadData2(RegReadData2));
  imm_gen imm_gen_1 (.Instruction(Instruction_P), .ImmSel(ImmSel), .Immediate(imm_gen_1_immediate));
  Multiplexer #(.enable("false"), .width(32)) multiplexer_4 (
    .in0(RegReadData1), .in1(ProgramCounter_P), .out(multiplexer_4_out), .sel(ASel));
  Multiplexer #(.enable("false"), .width(32)) multiplexer_5 (
    .in0(RegReadData2), .in1(imm_gen_1_immediate), .out(multiplexer_5_out), .sel(BSel));
  alu alu_1 (.ALUResult(MemAddress), .A(multiplexer_4_out), .B(multiplexer_5_out), .ALUSel(control_logic_1_alusel));
  partial_store partial_store_1 (
    .Instruction(Instruction_P), .MemAddress(MemAddress), .DataFromReg(RegReadData2), .MemWEn(MemWEn),
    .MemWriteMask(MemWriteMask), .DataToMem(MemWriteData));
  partial_load partial_load_1 (
    .Instruction(Instruction_P), .MemAddress(MemAddress), .DataFromMem(MemReadData), .DataToReg(ReadData));
  branch_comp branch_comp_1 (.BrData1(RegReadData1), .BrData2(RegReadData2), .BrUn(BrUn), .BrEq(BrEq), .BrLt(BrLt));

  // Other names for the same wires on the sheet: ALU_result[31:0] = MemAddress; rd[4:0] = Instruction_P[11:7];
  //   rs1[4:0] = Instruction_P[19:15]; rs2[4:0] = Instruction_P[24:20]

  // Notes on the sheet:
  //   To IMEM
  //   IMEM (do **NOT** move this)
  //   From IMEM
  //   Inputs/Outputs for testing. Do **NOT** move these.
  //   To DMEM
  //   DMEM (do **NOT** move this)
  //   From DMEM
endmodule
