// Logisim project partial-store.circ as structural Verilog: 1 circuit, main circuit partial_store
module partial_store (
  input  [31:0] Instruction,
  input  [31:0] MemAddress,
  input  [31:0] DataFromReg,
  input  MemWEn,
  output [3:0] MemWriteMask,
  output [31:0] DataToMem
);

  wire and_1_out, and_2_out, and_3_out, and_4_out, and_5_out, and_6_out, and_7_out, and_8_out, and_9_out,
       and_10_out, and_11_out, and_12_out, and_13_out, and_14_out, comparator_2_eq, comparator_3_eq,
       comparator_4_eq, comparator_5_eq, comparator_6_eq, comparator_7_eq, comparator_8_eq, comparator_9_eq,
       comparator_10_eq, comparator_11_eq, comparator_12_eq, comparator_13_eq, comparator_14_eq,
       comparator_15_eq, comparator_16_eq, comparator_17_eq, comparator_18_eq, comparator_19_eq,
       comparator_20_eq, comparator_21_eq, comparator_22_eq, comparator_23_eq, store;
  wire [31:0] bit_extender_1_out, bit_extender_2_out, bit_extender_3_out, bit_extender_4_out,
       multiplexer_1_out, multiplexer_2_out, multiplexer_3_out, multiplexer_4_out;

  Comparator #(.width(7)) comparator_1 (.a(Instruction[6:0]), .b(7'b0100011), .eq(store));  // open: gt, lt
  assign bit_extender_1_out = {{24{1'b0}}, DataFromReg[7:0]};  // Bit_Extender bit_extender_1
  assign bit_extender_2_out = {{16{1'b0}}, {DataFromReg[7:0], {8{1'b0}}}};  // Bit_Extender bit_extender_2
  assign bit_extender_3_out = {{8{1'b0}}, {DataFromReg[7:0], {16{1'b0}}}};  // Bit_Extender bit_extender_3
  assign bit_extender_4_out = {{16{1'b0}}, DataFromReg[15:0]};  // Bit_Extender bit_extender_4
  Comparator #(.width(7)) comparator_2 (.a(Instruction[6:0]), .b(7'b0100011), .eq(comparator_2_eq));  // open: gt, lt
  Comparator #(.width(3)) comparator_3 (.a(Instruction[14:12]), .b(3'b000), .eq(comparator_3_eq));  // open: gt, lt
  Comparator #(.width(7)) comparator_4 (.a(Instruction[6:0]), .b(7'b0100011), .eq(comparator_4_eq));  // open: gt, lt
  Comparator #(.width(3)) comparator_5 (.a(Instruction[14:12]), .b(3'b000), .eq(comparator_5_eq));  // open: gt, lt
  Comparator #(.width(7)) comparator_6 (.a(Instruction[6:0]), .b(7'b0100011), .eq(comparator_6_eq));  // open: gt, lt
  Comparator #(.width(3)) comparator_7 (.a(Instruction[14:12]), .b(3'b001), .eq(comparator_7_eq));  // open: gt, lt
  Comparator #(.width(7)) comparator_8 (.a(Instruction[6:0]), .b(7'b0100011), .eq(comparator_8_eq));  // open: gt, lt
  Comparator #(.width(3)) comparator_9 (.a(Instruction[14:12]), .b(3'b000), .eq(comparator_9_eq));  // open: gt, lt
  Comparator #(.width(7)) comparator_10 (.a(Instruction[6:0]), .b(7'b0100011), .eq(comparator_10_eq));  // open: gt, lt
  Comparator #(.width(3)) comparator_11 (.a(Instruction[14:12]), .b(3'b000), .eq(comparator_11_eq));  // open: gt, lt
  Comparator #(.width(7)) comparator_12 (.a(Instruction[6:0]), .b(7'b0100011), .eq(comparator_12_eq));  // open: gt, lt
  Comparator #(.width(3)) comparator_13 (.a(Instruction[14:12]), .b(3'b001), .eq(comparator_13_eq));  // open: gt, lt
  Comparator #(.width(7)) comparator_14 (.a(Instruction[6:0]), .b(7'b0100011), .eq(comparator_14_eq));  // open: gt, lt
  Comparator #(.width(3)) comparator_15 (.a(Instruction[14:12]), .b(3'b010), .eq(comparator_15_eq));  // open: gt, lt
  and and_1 (and_1_out, comparator_2_eq, comparator_3_eq);
  Comparator #(.width(2)) comparator_16 (.a(MemAddress[1:0]), .b(2'b00), .eq(comparator_16_eq));  // open: gt, lt
  and and_2 (and_2_out, comparator_4_eq, comparator_5_eq);
  Comparator #(.width(2)) comparator_17 (.a(MemAddress[1:0]), .b(2'b01), .eq(comparator_17_eq));  // open: gt, lt
  and and_3 (and_3_out, comparator_6_eq, comparator_7_eq);
  Comparator #(.width(2)) comparator_18 (.a(MemAddress[1:0]), .b(2'b00), .eq(comparator_18_eq));  // open: gt, lt
  and and_4 (and_4_out, comparator_8_eq, comparator_9_eq);
  Comparator #(.width(2)) comparator_19 (.a(MemAddress[1:0]), .b(2'b10), .eq(comparator_19_eq));  // open: gt, lt
  and and_5 (and_5_out, comparator_10_eq, comparator_11_eq);
  Comparator #(.width(2)) comparator_20 (.a(MemAddress[1:0]), .b(2'b11), .eq(comparator_20_eq));  // open: gt, lt
  and and_6 (and_6_out, comparator_12_eq, comparator_13_eq);
  Comparator #(.width(2)) comparator_21 (.a(MemAddress[1:0]), .b(2'b10), .eq(comparator_21_eq));  // open: gt, lt
  and and_7 (and_7_out, comparator_14_eq, comparator_15_eq);
  Comparator #(.width(2)) comparator_22 (.a(MemAddress[1:0]), .b(2'b00), .eq(comparator_22_eq));  // open: gt, lt
  Multiplexer #(.enable("false"), .select(2), .width(32)) multiplexer_1 (
    .in0(bit_extender_1_out), .in1(bit_extender_2_out), .in2(bit_extender_3_out),
    .in3({DataFromReg[7:0], {24{1'b0}}}), .out(multiplexer_1_out), .sel(MemAddress[1:0]));
  Multiplexer #(.enable("false"), .select(2), .width(32)) multiplexer_2 (
    .in0(bit_extender_4_out), .in2({DataFromReg[15:0], {16{1'b0}}}), .out(multiplexer_2_out),
    .sel(MemAddress[1:0]));  // open: in1, in3
  Multiplexer #(.enable("false"), .select(2), .width(32)) multiplexer_3 (
    .in0(DataFromReg), .out(multiplexer_3_out), .sel(MemAddress[1:0]));  // open: in1, in2, in3
  and and_8 (and_8_out, and_1_out, comparator_16_eq);
  and and_9 (and_9_out, and_2_out, comparator_17_eq);
  and and_10 (and_10_out, and_3_out, comparator_18_eq);
  and and_11 (and_11_out, and_4_out, comparator_19_eq);
  and and_12 (and_12_out, and_5_out, comparator_20_eq);
  and and_13 (and_13_out, and_6_out, comparator_21_eq);
  and and_14 (and_14_out, and_7_out, comparator_22_eq);
  Multiplexer #(.enable("false"), .select(3), .width(32)) multiplexer_4 (
    .in0(multiplexer_1_out), .in1(multiplexer_2_out), .in2(multiplexer_3_out), .out(multiplexer_4_out),
    .sel(Instruction[14:12]));  // open: in3, in4, in5, in6, in7
  Comparator #(.width(1)) comparator_23 (.a(MemWEn), .b(1'b0), .eq(comparator_23_eq));  // open: gt, lt
  Priority_Encoder #(.select(4)) priority_encoder_1 (
    .in0(comparator_23_eq), .in1(and_8_out), .in2(and_9_out), .in3(and_10_out), .in4(and_11_out),
    .in8(and_12_out), .in12(and_13_out), .in15(and_14_out), .out(MemWriteMask));  // open: in5, in6, in7, in9, in10, in11, in13, in14, gs, en_out, en_in
  Multiplexer #(.enable("false"), .width(32)) multiplexer_5 (
    .in1(multiplexer_4_out), .out(DataToMem), .sel(store));  // open: in0

  // Other names for the same wires on the sheet: byte[7:0] = DataFromReg[7:0]; half[15:0] = DataFromReg[15:0];
  //   word[31:0] = DataFromReg; opcode[6:0] = Instruction[6:0]; funct3[2:0] = Instruction[14:12];
  //   location[1:0] = MemAddress[1:0]

  // Notes on the sheet:
  //   INPUTS to your circuit
  //   DON'T CHANGE THE LOCATIONS OF THE INPUTS AND OUTPUTS!
  //   OUTPUT from your circuit
endmodule
