// Logisim project regfile.circ as structural Verilog: 1 circuit, main circuit regfile
module regfile (
  input  [4:0] ReadReg1,
  input  [4:0] ReadReg2,
  input  [4:0] WriteReg,
  input  [31:0] RegWriteData,
  input  RegWEn,
  input  clk,
  output [31:0] ra,
  output [31:0] sp,
  output [31:0] t0,
  output [31:0] t1,
  output [31:0] t2,
  output [31:0] s0,
  output [31:0] s1,
  output [31:0] a0,
  output [31:0] RegReadData1,
  output [31:0] RegReadData2
);

  wire x0, x1, x2, x3, x4, x5, x6, x7, x8, x9, x10, x11, x12, x13, x14, x15, x16, x17, x18, x19, x20, x21,
       x22, x23, x24, x25, x26, x27, x28, x29, x30, x31;
  wire [31:0] a1, a2, a3, a4, a5, a6, a7, gp, s2, s3, s4, s5, s6, s7, s8, s9, s10, s11, t3, t4, t5, t6, tp,
       v0;

  Demultiplexer #(.enable("false"), .select(5)) demultiplexer_1 (
    .out0(x0), .out1(x1), .out2(x2), .out3(x3), .out4(x4), .out5(x5), .out6(x6), .out7(x7), .out8(x8),
    .out9(x9), .out10(x10), .out11(x11), .out12(x12), .out13(x13), .out14(x14), .out15(x15), .out16(x16),
    .out17(x17), .out18(x18), .out19(x19), .out20(x20), .out21(x21), .out22(x22), .out23(x23), .out24(x24),
    .out25(x25), .out26(x26), .out27(x27), .out28(x28), .out29(x29), .out30(x30), .out31(x31), .in(RegWEn),
    .sel(WriteReg));
  Multiplexer #(.enable("false"), .select(5), .width(32)) multiplexer_1 (
    .in0(v0), .in1(ra), .in2(sp), .in3(gp), .in4(tp), .in5(t0), .in6(t1), .in7(t2), .in8(s0), .in9(s1),
    .in10(a0), .in11(a1), .in12(a2), .in13(a3), .in14(a4), .in15(a5), .in16(a6), .in17(a7), .in18(s2),
    .in19(s3), .in20(s4), .in21(s5), .in22(s6), .in23(s7), .in24(s8), .in25(s9), .in26(s10), .in27(s11),
    .in28(t3), .in29(t4), .in30(t5), .in31(t6), .out(RegReadData1), .sel(ReadReg1));
  Multiplexer #(.enable("false"), .select(5), .width(32)) multiplexer_2 (
    .in0(v0), .in1(ra), .in2(sp), .in3(gp), .in4(tp), .in5(t0), .in6(t1), .in7(t2), .in8(s0), .in9(s1),
    .in10(a0), .in11(a1), .in12(a2), .in13(a3), .in14(a4), .in15(a5), .in16(a6), .in17(a7), .in18(s2),
    .in19(s3), .in20(s4), .in21(s5), .in22(s6), .in23(s7), .in24(s8), .in25(s9), .in26(s10), .in27(s11),
    .in28(t3), .in29(t4), .in30(t5), .in31(t6), .out(RegReadData2), .sel(ReadReg2));
  Register #(.width(32)) u_x0 (.D({32{1'b0}}), .en(x0), .clk(clk), .Q(v0));  // open: clr
  Register #(.width(32)) x1_ra (.D(RegWriteData), .en(x1), .clk(clk), .Q(ra));  // open: clr
  Register #(.width(32)) x7_t2 (.D(RegWriteData), .en(x7), .clk(clk), .Q(t2));  // open: clr
  Register #(.width(32)) x13_a3 (.D(RegWriteData), .en(x13), .clk(clk), .Q(a3));  // open: clr
  Register #(.width(32)) x19_s3 (.D(RegWriteData), .en(x19), .clk(clk), .Q(s3));  // open: clr
  Register #(.width(32)) x25_s9 (.D(RegWriteData), .en(x25), .clk(clk), .Q(s9));  // open: clr
  Register #(.width(32)) x31_t6 (.D(RegWriteData), .en(x31), .clk(clk), .Q(t6));  // open: clr
  Register #(.width(32)) x2_sp (.D(RegWriteData), .en(x2), .clk(clk), .Q(sp));  // open: clr
  Register #(.width(32)) x8_s0 (.D(RegWriteData), .en(x8), .clk(clk), .Q(s0));  // open: clr
  Register #(.width(32)) x14_a4 (.D(RegWriteData), .en(x14), .clk(clk), .Q(a4));  // open: clr
  Register #(.width(32)) x20_s4 (.D(RegWriteData), .en(x20), .clk(clk), .Q(s4));  // open: clr
  Register #(.width(32)) x26_s10 (.D(RegWriteData), .en(x26), .clk(clk), .Q(s10));  // open: clr
  Register #(.width(32)) x3_gp (.D(RegWriteData), .en(x3), .clk(clk), .Q(gp));  // open: clr
  Register #(.width(32)) x9_s1 (.D(RegWriteData), .en(x9), .clk(clk), .Q(s1));  // open: clr
  Register #(.width(32)) x15_a5 (.D(RegWriteData), .en(x15), .clk(clk), .Q(a5));  // open: clr
  Register #(.width(32)) x21_s5 (.D(RegWriteData), .en(x21), .clk(clk), .Q(s5));  // open: clr
  Register #(.width(32)) x27_s11 (.D(RegWriteData), .en(x27), .clk(clk), .Q(s11));  // open: clr
  Register #(.width(32)) x4_tp (.D(RegWriteData), .en(x4), .clk(clk), .Q(tp));  // open: clr
  Register #(.width(32)) x10_a0 (.D(RegWriteData), .en(x10), .clk(clk), .Q(a0));  // open: clr
  Register #(.width(32)) x16_a6 (.D(RegWriteData), .en(x16), .clk(clk), .Q(a6));  // open: clr
  Register #(.width(32)) x22_s6 (.D(RegWriteData), .en(x22), .clk(clk), .Q(s6));  // open: clr
  Register #(.width(32)) x28_t3 (.D(RegWriteData), .en(x28), .clk(clk), .Q(t3));  // open: clr
  Register #(.width(32)) x5_t0 (.D(RegWriteData), .en(x5), .clk(clk), .Q(t0));  // open: clr
  Register #(.width(32)) x11_a1 (.D(RegWriteData), .en(x11), .clk(clk), .Q(a1));  // open: clr
  Register #(.width(32)) x17_a7 (.D(RegWriteData), .en(x17), .clk(clk), .Q(a7));  // open: clr
  Register #(.width(32)) x23_s7 (.D(RegWriteData), .en(x23), .clk(clk), .Q(s7));  // open: clr
  Register #(.width(32)) x29_t4 (.D(RegWriteData), .en(x29), .clk(clk), .Q(t4));  // open: clr
  Register #(.width(32)) x6_t1 (.D(RegWriteData), .en(x6), .clk(clk), .Q(t1));  // open: clr
  Register #(.width(32)) x12_a2 (.D(RegWriteData), .en(x12), .clk(clk), .Q(a2));  // open: clr
  Register #(.width(32)) x18_s2 (.D(RegWriteData), .en(x18), .clk(clk), .Q(s2));  // open: clr
  Register #(.width(32)) x24_s8 (.D(RegWriteData), .en(x24), .clk(clk), .Q(s8));  // open: clr
  Register #(.width(32)) x30_t5 (.D(RegWriteData), .en(x30), .clk(clk), .Q(t5));  // open: clr

  // Notes on the sheet:
  //   INPUTS to your circuit
  //   DON'T CHANGE THE LOCATIONS OF THE INPUTS AND OUTPUTS!
  //   These are DEBUG/TEST outputs from your circuit.
  //   OUTPUTS from your circuit
endmodule
